# Fritzing sketch Radio sketch (saved by Fritzing 0.9.2b)
perfboards: 1

parts:
  Part1 = Arduino Nano (Rev3.0)
  4_5_Volt_(3_x_AA) = Battery Holders [package=battery-aa-kit]
  U1 = SWITCH_SPDT [package=kps-1290]
  S2 = Pushbutton [package=THT]  # not connected
  S3 = Pushbutton [package=THT]
  S4 = Pushbutton [package=THT]  # not connected
  S5 = Pushbutton [package=THT]
  S6 = Pushbutton [package=THT]
  S7 = Pushbutton [package=THT]
  S8 = Pushbutton [package=THT]
  S9 = Pushbutton [package=THT]
  Part2 = Adafruit 4-channel I2C-safe Bi-directional Logic Level Converter [part_number="Adafruit #757"]
  Sparkfun_Si4703_basic_breakout = Digital FM Radio Receiver
  OLED_0_96"_128x64_I2C_display = OLED Monochrome 128x32 I2C [part_number=931]

nets:
  GND: Part1.GND, 4_5_Volt_(3_x_AA).-, Part2.GND, Sparkfun_Si4703_basic_breakout.GND, OLED_0_96"_128x64_I2C_display.GND
  N1: Part1.D2, Part2.B3
  N2: Part1.D9, S6.leg0
  N3: Part1.D10, S7.leg0
  N4: Part1.D11/MOSI, S8.leg0
  N5: Part1.D12/MISO, S9.leg0
  N6: Part1.5V, U1.O, Part2.HV
  N7: Part1.A5, Part2.B2
  N8: Part1.A4, Part2.B1
  3V3: Part1.3V3, Part2.LV, Sparkfun_Si4703_basic_breakout.3.3V, OLED_0_96"_128x64_I2C_display.VIN
  N9: 4_5_Volt_(3_x_AA).+, U1.P
  N10: S3.leg1, S5.leg1
  N11: Part2.A3, Sparkfun_Si4703_basic_breakout.!RST
  N12: Part2.A2, Sparkfun_Si4703_basic_breakout.SCLK, OLED_0_96"_128x64_I2C_display.SCL
  N13: Part2.A1, Sparkfun_Si4703_basic_breakout.SDIO, OLED_0_96"_128x64_I2C_display.SDA

notes:
  Nano A4: SDA
  Nano A5: SCL
  Nano D2: RST

custom parts:
  Adafruit 4-channel I2C-safe Bi-directional Logic Level Converter: Because the Arduino (and Basic Stamp) are 5V devices, and most modern sensors, displays, flash cards and modes are 3.3V-only, many makers find that they need to perform level shifting/conversion to protect the 3.3V device from 5V. We do have some other handy level shifters in the shop, from the DIP 74LVC245 to the fancy bi-directional TXB0108. However, neither of these are happy to work with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
  OLED Monochrome 128x32 I2C: These displays are small, only about 1" diagonal, but very readable due to the high contrast of an OLED display. This display is made of 128x32 individual white OLED pixels, each one is turned on or off by the controller chip. Because the display makes its own light, no backlight is required. This reduces the power required to run the OLED and is why the display has such high contrast; we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
